// Logisim project xora.circ as structural Verilog: 3 circuits, main circuit main
module main (
);

  drive_256_MiB drive_256_mib_1 ();  // open: CLK, DATA, DATA_out, device_is_ready
endmodule

module drive_256_MiB (
  input  CLK,
  input  [7:0] DATA,
  output [7:0] DATA_out,
  output device_is_ready
);

  wire adder_1_cout, and_1_out, and_2_out, and_3_out, and_4_out, and_5_out, and_6_out, and_7_out, and_8_out,
       and_11_out, and_13_out, and_14_out, and_15_out, buffer_1_out, buffer_2_out, buffer_3_out,
       buffer_4_out, buffer_5_out, buffer_6_out, buffer_7_out, buffer_8_out, buffer_9_out, decoder_1_out0,
       decoder_1_out1, decoder_1_out2, decoder_1_out3, decoder_1_out4, decoder_1_out5, decoder_1_out6,
       decoder_1_out7, decoder_1_out8, decoder_1_out9, decoder_1_out10, decoder_1_out11, decoder_1_out12,
       decoder_1_out13, decoder_1_out14, decoder_1_out15, decoder_2_out0, decoder_2_out1, decoder_2_out2,
       decoder_2_out3, not_1_out, not_2_out, not_3_out, not_4_out, not_5_out, not_6_out, not_7_out,
       not_8_out, not_9_out, not_10_out, or_1_out, or_2_out, or_3_out, or_4_out, or_5_out, or_6_out,
       or_8_out, pull_resistor_2_node, pull_resistor_6_node, pull_resistor_8_node, pull_resistor_13_node,
       pull_resistor_14_node, pull_resistor_25_node, s_r_ff_1_q, s_r_ff_2_q, s_r_ff_4_q, s_r_ff_5_q,
       t_ff_1_q, t_ff_3_q;
  wire [1:0] pull_resistor_3_node;
  wire [2:0] counter_2_q;
  wire [3:0] counter_3_q, pull_resistor_4_node, pull_resistor_7_node, pull_resistor_9_node,
       pull_resistor_9_node_2, pull_resistor_9_node_3, pull_resistor_9_node_4, pull_resistor_9_node_5,
       pull_resistor_9_node_6;
  wire [4:4] t_ff_2_q;
  wire [5:0] pull_resistor_1_node;
  wire [7:0] ram_1_dout, ram_2_dout, ram_3_dout, ram_4_dout, ram_5_dout, ram_6_dout, ram_7_dout, ram_8_dout,
       ram_9_dout, ram_10_dout, ram_11_dout, ram_12_dout, ram_13_dout, ram_14_dout, ram_15_dout, ram_16_dout,
       register_1_q, register_2_q, register_3_q, register_4_q, rom_1_data;
  wire [9:9] pull_resistor_22_node;
  wire [11:0] pla_4_out;
  wire [15:0] pla_3_out;
  wire [31:0] counter_1_q, multiplier_1_out;

  buf buffer_1 (buffer_1_out, pull_resistor_1_node[0]);
  buf buffer_2 (buffer_2_out, pull_resistor_3_node[1]);
  buf buffer_3 (buffer_3_out, pull_resistor_13_node);
  Pull_Resistor pull_resistor_1 (.node(pull_resistor_1_node[0]));
  buf buffer_4 (buffer_4_out, pull_resistor_1_node[0]);
  buf buffer_5 (buffer_5_out, pull_resistor_13_node);
  not not_1 (not_1_out, buffer_5_out);
  buf buffer_6 (buffer_6_out, pull_resistor_1_node[0]);
  not not_2 (not_2_out, buffer_6_out);
  and and_1 (and_1_out, pull_resistor_1_node[0], not_3_out);
  not not_3 (not_3_out, buffer_1_out);
  and and_2 (and_2_out, pull_resistor_3_node[1], not_4_out);
  not not_4 (not_4_out, buffer_2_out);
  and and_3 (and_3_out, pull_resistor_13_node, not_5_out);
  not not_5 (not_5_out, buffer_3_out);
  and and_4 (and_4_out, pull_resistor_1_node[0], not_6_out);
  not not_6 (not_6_out, buffer_4_out);
  and and_5 (and_5_out, pull_resistor_13_node, not_1_out);
  and and_6 (and_6_out, pull_resistor_1_node[0], not_2_out);
  and and_7 (and_7_out, pull_resistor_2_node, CLK);
  Pull_Resistor pull_resistor_2 (.node(pull_resistor_2_node));
  or or_1 (or_1_out, and_1_out, and_2_out);
  S_R_Flip_Flop s_r_ff_1 (.S(and_3_out), .R(and_4_out), .clk(or_2_out), .Q(s_r_ff_1_q));  // open: reset, Qn, preset
  or or_2 (or_2_out, and_3_out, and_4_out);
  S_R_Flip_Flop s_r_ff_2 (.S(and_5_out), .R(and_6_out), .clk(or_3_out), .Q(s_r_ff_2_q));  // open: reset, Qn, preset
  or or_3 (or_3_out, and_5_out, and_6_out);
  Decoder #(.select(4)) decoder_1 (
    .out0(decoder_1_out0), .out1(decoder_1_out1), .out2(decoder_1_out2), .out3(decoder_1_out3),
    .out4(decoder_1_out4), .out5(decoder_1_out5), .out6(decoder_1_out6), .out7(decoder_1_out7),
    .out8(decoder_1_out8), .out9(decoder_1_out9), .out10(decoder_1_out10), .out11(decoder_1_out11),
    .out12(decoder_1_out12), .out13(decoder_1_out13), .out14(decoder_1_out14), .out15(decoder_1_out15),
    .sel(pull_resistor_4_node), .en(and_7_out));
  Pull_Resistor pull_resistor_3 (.node(pull_resistor_3_node));
  and and_8 (and_8_out, CLK, pull_resistor_2_node);
  S_R_Flip_Flop s_r_ff_3 (
    .S(and_1_out), .R(and_2_out), .clk(or_1_out), .Q(pull_resistor_2_node));  // open: reset, Qn, preset
  Pull_Resistor pull_resistor_4 (.node(pull_resistor_4_node));
  Counter #(.max('hffffffff), .width(32)) counter_1 (
    .clr(pull_resistor_3_node[1]), .clk(and_8_out), .Q(counter_1_q));  // open: load, up, count, D, carry
  Pull_Resistor pull_resistor_5 (.node(s_r_ff_1_q));
  Pull_Resistor pull_resistor_6 (.node(pull_resistor_6_node));
  and and_9 (pull_resistor_6_node, CLK, not_7_out);
  not not_7 (not_7_out, buffer_7_out);
  buf buffer_7 (buffer_7_out, CLK);
  Pull_Resistor pull_resistor_7 (.node(pull_resistor_7_node));
  Counter #(.max('h7), .width(3)) counter_2 (
    .clr(pull_resistor_1_node[0]), .clk(pull_resistor_8_node), .Q(counter_2_q));  // open: load, up, count, D, carry
  Pull_Resistor pull_resistor_8 (.node(pull_resistor_8_node));
  and and_10 (pull_resistor_8_node, s_r_ff_1_q, pull_resistor_6_node);
  PLA #(.in_width(32), .\table ("00000000000000000001000000000000 10")) pla_1 (
    .in(counter_1_q), .out(pull_resistor_3_node));
  Pull_Resistor pull_resistor_9 (.node({pull_resistor_9_node_6, pull_resistor_9_node_5, pull_resistor_9_node_4, pull_resistor_9_node_3, pull_resistor_9_node_2, pull_resistor_9_node}));
  buf buffer_8 (buffer_8_out, s_r_ff_1_q);
  PLA #(.in_width(3), .out_width(6), .\table ("100 000001")) pla_2 (.in(counter_2_q), .out(pull_resistor_1_node));
  RAM #(.addrWidth(24), .enables("line")) ram_1 (
    .addr({pull_resistor_9_node_6, pull_resistor_9_node_5, pull_resistor_9_node_4, pull_resistor_9_node_3, pull_resistor_9_node_2, pull_resistor_9_node}),
    .we(s_r_ff_4_q), .clk(decoder_1_out0), .din(DATA), .dout(ram_1_dout));
  RAM #(.addrWidth(24), .enables("line")) ram_2 (
    .addr({pull_resistor_9_node_6, pull_resistor_9_node_5, pull_resistor_9_node_4, pull_resistor_9_node_3, pull_resistor_9_node_2, pull_resistor_9_node}),
    .we(s_r_ff_4_q), .clk(decoder_1_out1), .din(DATA), .dout(ram_2_dout));
  RAM #(.addrWidth(24), .enables("line")) ram_3 (
    .addr({pull_resistor_9_node_6, pull_resistor_9_node_5, pull_resistor_9_node_4, pull_resistor_9_node_3, pull_resistor_9_node_2, pull_resistor_9_node}),
    .we(s_r_ff_4_q), .clk(decoder_1_out2), .din(DATA), .dout(ram_3_dout));
  RAM #(.addrWidth(24), .enables("line")) ram_4 (
    .addr({pull_resistor_9_node_6, pull_resistor_9_node_5, pull_resistor_9_node_4, pull_resistor_9_node_3, pull_resistor_9_node_2, pull_resistor_9_node}),
    .we(s_r_ff_4_q), .clk(decoder_1_out3), .din(DATA), .dout(ram_4_dout));
  Pull_Resistor pull_resistor_10 (.node(pull_resistor_3_node[1]));
  or or_4 (or_4_out, pull_resistor_3_node[1], pla_3_out[3]);
  Pull_Resistor pull_resistor_11 (.node(pull_resistor_3_node[1]));
  or or_5 (or_5_out, pla_3_out[4], pull_resistor_3_node[1]);
  and and_11 (and_11_out, s_r_ff_1_q, not_8_out);
  not not_8 (not_8_out, buffer_8_out);
  Pull_Resistor pull_resistor_12 (.node(pull_resistor_3_node[1]));
  S_R_Flip_Flop s_r_ff_4 (
    .S(pla_3_out[3]), .R(pull_resistor_3_node[1]), .clk(or_4_out), .Q(s_r_ff_4_q));  // open: reset, Qn, preset
  S_R_Flip_Flop s_r_ff_5 (
    .S(pla_3_out[4]), .R(pull_resistor_3_node[1]), .clk(or_5_out), .Q(s_r_ff_5_q));  // open: reset, Qn, preset
  Pull_Resistor pull_resistor_13 (.node(pull_resistor_13_node));
  Multiplier #(.width(32)) multiplier_1 (
    .a(32'h1000), .b({register_4_q, register_3_q, register_2_q, register_1_q}), .out(multiplier_1_out));  // open: cin, cout
  or or_6 (or_6_out, and_11_out, pull_resistor_3_node[1]);
  or or_7 (pull_resistor_13_node, s_r_ff_4_q, s_r_ff_5_q);
  Pull_Resistor pull_resistor_14 (.node(pull_resistor_14_node));
  Adder #(.width(32)) adder_1 (
    .a(counter_1_q), .b(multiplier_1_out),
    .out({pull_resistor_7_node, pull_resistor_4_node, pull_resistor_9_node_6, pull_resistor_9_node_5, pull_resistor_9_node_4, pull_resistor_9_node_3, pull_resistor_9_node_2, pull_resistor_9_node}),
    .cin(pull_resistor_14_node), .cout(adder_1_cout));
  Pull_Resistor pull_resistor_15 (.node(s_r_ff_4_q));
  Pull_Resistor pull_resistor_16 (.node(adder_1_cout));
  Decoder #(.select(2)) decoder_2 (
    .out0(decoder_2_out0), .out1(decoder_2_out1), .out2(decoder_2_out2), .out3(decoder_2_out3),
    .sel(counter_2_q[1:0]), .en(s_r_ff_2_q));
  Pull_Resistor pull_resistor_17 (.node(ram_1_dout));
  Pull_Resistor pull_resistor_18 (.node(ram_2_dout));
  Pull_Resistor pull_resistor_19 (.node(ram_3_dout));
  Pull_Resistor pull_resistor_20 (.node(ram_4_dout));
  // LedBar #(.inputtype("row"), .matrixcols(32)) ledbar_1: pin names not known; wires that end beside it: {pull_resistor_7_node, pull_resistor_4_node, pull_resistor_9_node_6, pull_resistor_9_node_5, pull_resistor_9_node_4, pull_resistor_9_node_3, pull_resistor_9_node_2, pull_resistor_9_node}
  Pull_Resistor pull_resistor_21 (.node(CLK));
  Pull_Resistor pull_resistor_22 (.node(pull_resistor_22_node[9]));
  assign DATA_out = and_15_out ? rom_1_data : 8'bz;  // Controlled_Buffer controlled_buffer_1
  Register register_1 (.D(DATA), .en(decoder_2_out0), .clk(CLK), .Q(register_1_q));  // open: clr
  Register register_2 (.D(DATA), .en(decoder_2_out1), .clk(CLK), .Q(register_2_q));  // open: clr
  Register register_3 (.D(DATA), .en(decoder_2_out2), .clk(CLK), .Q(register_3_q));  // open: clr
  Register register_4 (.D(DATA), .en(decoder_2_out3), .clk(CLK), .Q(register_4_q));  // open: clr
  Pull_Resistor pull_resistor_23 (.node(DATA_out));
  Pull_Resistor pull_resistor_24 (.node(device_is_ready));
  Pull_Resistor pull_resistor_25 (.node(pull_resistor_25_node));
  and and_12 (pull_resistor_25_node, CLK, t_ff_1_q);
  RAM #(.addrWidth(24), .enables("line")) ram_5 (
    .addr({pull_resistor_9_node_6, pull_resistor_9_node_5, pull_resistor_9_node_4, pull_resistor_9_node_3, pull_resistor_9_node_2, pull_resistor_9_node}),
    .we(s_r_ff_4_q), .clk(decoder_1_out4), .din(DATA), .dout(ram_5_dout));
  RAM #(.addrWidth(24), .enables("line")) ram_6 (
    .addr({pull_resistor_9_node_6, pull_resistor_9_node_5, pull_resistor_9_node_4, pull_resistor_9_node_3, pull_resistor_9_node_2, pull_resistor_9_node}),
    .we(s_r_ff_4_q), .clk(decoder_1_out5), .din(DATA), .dout(ram_6_dout));
  RAM #(.addrWidth(24), .enables("line")) ram_7 (
    .addr({pull_resistor_9_node_6, pull_resistor_9_node_5, pull_resistor_9_node_4, pull_resistor_9_node_3, pull_resistor_9_node_2, pull_resistor_9_node}),
    .we(s_r_ff_4_q), .clk(decoder_1_out6), .din(DATA), .dout(ram_7_dout));
  RAM #(.addrWidth(24), .enables("line")) ram_8 (
    .addr({pull_resistor_9_node_6, pull_resistor_9_node_5, pull_resistor_9_node_4, pull_resistor_9_node_3, pull_resistor_9_node_2, pull_resistor_9_node}),
    .we(s_r_ff_4_q), .clk(decoder_1_out7), .din(DATA), .dout(ram_8_dout));
  not not_9 (not_9_out, CLK);
  not not_10 (not_10_out, not_9_out);
  PLA #(.in_width(12), .out_width(16), .\table ("110000000011 0000000000000001 # get device type\n110000000001 0000000000001000 # Write\n110000000010 0000000000010000 # Read")) pla_3 (
    .in({device_is_ready, CLK, {2{pull_resistor_22_node[9]}}, DATA}), .out(pla_3_out));
  and and_13 (and_13_out, pla_3_out[1], pla_4_out[8]);
  Pull_Resistor pull_resistor_26 (.node(ram_5_dout));
  Pull_Resistor pull_resistor_27 (.node(ram_6_dout));
  Pull_Resistor pull_resistor_28 (.node(ram_7_dout));
  T_Flip_Flop t_ff_1 (.T(or_8_out), .clk(buffer_9_out), .Q(t_ff_1_q), .Qn(device_is_ready));  // open: reset, preset
  or or_8 (or_8_out, pla_4_out[9], or_6_out, and_13_out);
  buf buffer_9 (buffer_9_out, or_8_out);
  Pull_Resistor pull_resistor_29 (.node(ram_8_dout));
  Multiplexer #(.enable("true"), .select(4), .width(8)) multiplexer_1 (
    .in0(ram_1_dout), .in1(ram_2_dout), .in2(ram_3_dout), .in3(ram_4_dout), .in4(ram_5_dout),
    .in5(ram_6_dout), .in6(ram_7_dout), .in7(ram_8_dout), .in8(ram_9_dout), .in9(ram_10_dout),
    .in10(ram_11_dout), .in11(ram_12_dout), .in12(ram_13_dout), .in13(ram_14_dout), .in14(ram_15_dout),
    .in15(ram_16_dout), .out(DATA_out), .sel(pull_resistor_4_node), .en(s_r_ff_5_q));
  T_Flip_Flop t_ff_2 (.Q(t_ff_2_q[4]), .reset(pla_4_out[11]), .preset(pla_3_out[2]));  // open: T, clk, Qn
  T_Flip_Flop t_ff_3 (.T(pla_3_out[0]), .clk(not_10_out), .Q(t_ff_3_q), .reset(pla_4_out[11]));  // open: Qn, preset
  and and_14 (and_14_out, not_10_out, t_ff_3_q);
  and and_15 (and_15_out, t_ff_3_q, pla_4_out[10]);
  RAM #(.addrWidth(24), .enables("line")) ram_9 (
    .addr({pull_resistor_9_node_6, pull_resistor_9_node_5, pull_resistor_9_node_4, pull_resistor_9_node_3, pull_resistor_9_node_2, pull_resistor_9_node}),
    .we(s_r_ff_4_q), .clk(decoder_1_out8), .din(DATA), .dout(ram_9_dout));
  RAM #(.addrWidth(24), .enables("line")) ram_10 (
    .addr({pull_resistor_9_node_6, pull_resistor_9_node_5, pull_resistor_9_node_4, pull_resistor_9_node_3, pull_resistor_9_node_2, pull_resistor_9_node}),
    .we(s_r_ff_4_q), .clk(decoder_1_out9), .din(DATA), .dout(ram_10_dout));
  RAM #(.addrWidth(24), .enables("line")) ram_11 (
    .addr({pull_resistor_9_node_6, pull_resistor_9_node_5, pull_resistor_9_node_4, pull_resistor_9_node_3, pull_resistor_9_node_2, pull_resistor_9_node}),
    .we(s_r_ff_4_q), .clk(decoder_1_out10), .din(DATA), .dout(ram_11_dout));
  RAM #(.addrWidth(24), .enables("line")) ram_12 (
    .addr({pull_resistor_9_node_6, pull_resistor_9_node_5, pull_resistor_9_node_4, pull_resistor_9_node_3, pull_resistor_9_node_2, pull_resistor_9_node}),
    .we(s_r_ff_4_q), .clk(decoder_1_out11), .din(DATA), .dout(ram_12_dout));
  Counter #(.max('hf), .width(4)) counter_3 (
    .clr(pla_4_out[11]), .clk(and_14_out), .Q(counter_3_q));  // open: load, up, count, D, carry
  ROM #(.addrWidth(4)) rom_1 (.addr(counter_3_q), .data(rom_1_data));
  Pull_Resistor pull_resistor_30 (.node(ram_9_dout));
  Pull_Resistor pull_resistor_31 (.node(ram_10_dout));
  Pull_Resistor pull_resistor_32 (.node(ram_11_dout));
  Pull_Resistor pull_resistor_33 (.node(ram_12_dout));
  PLA #(.in_width(5), .out_width(12), .\table ("00101 101000000000\n000xx 010100000000\n10000 000000000000\n10000 000000000000")) pla_4 (
    .in({t_ff_2_q[4], counter_3_q}), .out(pla_4_out));
  RAM #(.addrWidth(24), .enables("line")) ram_13 (
    .addr({pull_resistor_9_node_6, pull_resistor_9_node_5, pull_resistor_9_node_4, pull_resistor_9_node_3, pull_resistor_9_node_2, pull_resistor_9_node}),
    .we(s_r_ff_4_q), .clk(decoder_1_out12), .din(DATA), .dout(ram_13_dout));
  RAM #(.addrWidth(24), .enables("line")) ram_14 (
    .addr({pull_resistor_9_node_6, pull_resistor_9_node_5, pull_resistor_9_node_4, pull_resistor_9_node_3, pull_resistor_9_node_2, pull_resistor_9_node}),
    .we(s_r_ff_4_q), .clk(decoder_1_out13), .din(DATA), .dout(ram_14_dout));
  RAM #(.addrWidth(24), .enables("line")) ram_15 (
    .addr({pull_resistor_9_node_6, pull_resistor_9_node_5, pull_resistor_9_node_4, pull_resistor_9_node_3, pull_resistor_9_node_2, pull_resistor_9_node}),
    .we(s_r_ff_4_q), .clk(decoder_1_out14), .din(DATA), .dout(ram_15_dout));
  RAM #(.addrWidth(24), .enables("line")) ram_16 (
    .addr({pull_resistor_9_node_6, pull_resistor_9_node_5, pull_resistor_9_node_4, pull_resistor_9_node_3, pull_resistor_9_node_2, pull_resistor_9_node}),
    .we(s_r_ff_4_q), .clk(decoder_1_out15), .din(DATA), .dout(ram_16_dout));
  Pull_Resistor pull_resistor_34 (.node(ram_13_dout));
  Pull_Resistor pull_resistor_35 (.node(ram_14_dout));
  Pull_Resistor pull_resistor_36 (.node(ram_15_dout));
  Pull_Resistor pull_resistor_37 (.node(ram_16_dout));

  // Notes on the sheet:
  //   contents of rom_1 (hex, n*v repeats v):
  //   3 1 0 3 ff ff
endmodule

module CPU (
  input  WRITE,
  input  READ,
  input  clk,
  input  [7:0] DATA,
  input  INTERUPT,
  output IO_CLK,
  output IO_SELECT,
  output [7:0] DATA_OUT,
  output [23:0] ADDRESS
);

  Pull_Resistor pull_resistor_1 (.node(DATA_OUT));
  Pull_Resistor pull_resistor_2 (.node(ADDRESS));
endmodule
